// Logisim project lab_04.circ as structural Verilog
module ex_01_a (
  input  Set,
  input  Reset,
  input  in_3,
  input  in_4,
  output out_5,
  output out_6,
  output out_7,
  output out_8
);

  nand nand_1 (out_5, Set, out_6);
  nand nand_2 (out_6, out_5, Reset);
  latch_nand latch_nand_1 (.S(in_3), .R(in_4), .Q(out_7), .QN(out_8));

  // Notes on the sheet:
  //   Latch SR NAND
endmodule

module ex_01_b (
  input  Set_2,
  input  Reset_2,
  input  in_3,
  input  in_4,
  output out_5,
  output out_6,
  output out_7,
  output out_8
);

  nor nor_1 (out_5, Set_2, out_6);
  nor nor_2 (out_6, out_5, Reset_2);
  latch_nor latch_nor_1 (.S(in_3), .R(in_4), .Q(out_7), .QN(out_8));

  // Notes on the sheet:
  //   Latch SR NOR
endmodule

module ex_02_a (
  input  D,
  input  Enable,
  output Q,
  output QN
);

  wire nand_1_out, nand_2_out, not_1_out;

  not not_1 (not_1_out, D);
  nand nand_1 (nand_1_out, D, Enable);
  nand nand_2 (nand_2_out, Enable, not_1_out);
  nand nand_3 (Q, nand_1_out, QN);
  nand nand_4 (QN, Q, nand_2_out);

  // Notes on the sheet:
  //   Latch D NAND
endmodule

module ex_03_a (
  input  CLK,
  input  J,
  input  K,
  output out_4
);

  wire and_1_out, and_2_out, not_1_out, not_2_out, undriven;

  not not_1 (not_1_out, undriven);
  not not_2 (not_2_out, K);
  and and_1 (and_1_out, J, not_1_out);
  buf and_2 (and_2_out, not_2_out);  // AND_Gate
  // OR_Gate or_1 has open pins: in0=and_1_out, in1=and_2_out, out=open
endmodule

module ex_02_b (
  input  D,
  input  Enable,
  output Q,
  output QN
);

  wire nor_1_out, nor_2_out, not_1_out;

  not not_1 (not_1_out, D);
  nor nor_1 (nor_1_out, D, Enable);
  nor nor_2 (nor_2_out, Enable, not_1_out);
  nor nor_3 (Q, nor_1_out, QN);
  nor nor_4 (QN, Q, nor_2_out);
endmodule

// VHDL entity latch_nand, as the project stores it:
--------------------------------------------------------------------------------
-- Project :
-- File    :
-- Autor   :
-- Date    :
--
--------------------------------------------------------------------------------
-- Description :
--
--------------------------------------------------------------------------------

LIBRARY ieee;
USE ieee.std_logic_1164.all;

ENTITY latch_nand IS
  PORT (
  ------------------------------------------------------------------------------
  --Insert input ports below
    S,R      : IN  std_logic;                    
  ------------------------------------------------------------------------------
  --Insert output ports below
    Q,QN        : OUT std_logic                

    );
END latch_nand;

--------------------------------------------------------------------------------
--Complete your VHDL description below
--------------------------------------------------------------------------------

ARCHITECTURE TypeArchitecture OF latch_nand IS
SIGNAL qstate : std_logic;

BEGIN
  PROCESS(S,R)
  BEGIN
    IF (S = '1' AND R = '0') THEN
      qstate <= '1';
    ELSIF (S = '0' AND R = '1') THEN
      qstate <= '0';
    END IF;
  END PROCESS;

  Q <= qstate;
  QN <= NOT qstate;

END TypeArchitecture;

// VHDL entity latch_nor, as the project stores it:
--------------------------------------------------------------------------------
-- Project :
-- File    :
-- Autor   :
-- Date    :
--
--------------------------------------------------------------------------------
-- Description :
--
--------------------------------------------------------------------------------

LIBRARY ieee;
USE ieee.std_logic_1164.all;

ENTITY latch_nor IS
  PORT (
  ------------------------------------------------------------------------------
  --Insert input ports below
    S,R      : IN  std_logic;                    
  ------------------------------------------------------------------------------
  --Insert output ports below
    Q,QN        : OUT std_logic              

    );
END latch_nor;

--------------------------------------------------------------------------------
--Complete your VHDL description below
--------------------------------------------------------------------------------

ARCHITECTURE TypeArchitecture OF latch_nor IS
SIGNAL qstate : std_logic;

BEGIN
  PROCESS(S,R)
  BEGIN
    IF (S = '1' AND R = '0') THEN
      qstate <= '1';
    ELSIF (S = '0' AND R = '1') THEN
      qstate <= '0';
    END IF;
  END PROCESS;

  Q <= qstate;
  QN <= NOT qstate;

END TypeArchitecture;

// VHDL entity latch_d_nand, as the project stores it:
--------------------------------------------------------------------------------
-- Project :
-- File    :
-- Autor   :
-- Date    :
--
--------------------------------------------------------------------------------
-- Description :
--
--------------------------------------------------------------------------------

LIBRARY ieee;
USE ieee.std_logic_1164.all;

ENTITY latch_d_nand IS
  PORT (
  ------------------------------------------------------------------------------
  --Insert input ports below
    enable,din      : IN  std_logic;                    
  ------------------------------------------------------------------------------
  --Insert output ports below
    q        : OUT std_logic       
    );
END latch_d_nand;

--------------------------------------------------------------------------------
--Complete your VHDL description below
--------------------------------------------------------------------------------

ARCHITECTURE TypeArchitecture OF latch_d_nand IS

BEGIN
	PROCESS(enable,din)
	begin
		if enable = '1' then q <= din;
		end if;
  END PROCESS;

END TypeArchitecture;
