// Logisim project Aula_03_ex_01.circ as structural Verilog
module main (
  input  [3:0] in_1
);

  wire undriven, undriven_2, undriven_3, undriven_4, undriven_5;
  wire [1:0] undriven_6;

  dec_7s_muxes dec_7s_muxes_1 ();
  _7_Segment_Display u_7_segment_display_1 (
    .g(undriven_6[0]), .f(undriven_6[1]), .a(undriven), .b(undriven_2), .e(undriven_5), .d(undriven_4),
    .c(undriven_3));  // open: dp
endmodule
